# Fritzing sketch plan (saved by Fritzing 0.9.3b)
breadboards: 2

parts:
  Part1 = Arduino Uno (Rev3)
  Raspberry_Pi1 = Raspberry Pi B+
  M1 = RioRand LM2596
  M2 = DC Motor
  M3 = DC Motor
  J2 = Basic Servo
  J3 = Basic Servo
  Part2 = IFR520 MOS module [package=THT]
  BAT1 = Battery Holders [package=lipo-1100mAh]
  BAT2 = Battery Holders [package=lipo-1100mAh]  # not connected
  BAT3 = Battery Holders [package=lipo-1100mAh]  # not connected
  BAT4 = Battery Holders [package=lipo-1100mAh]
  LED1 = smd LED [color="Red (633nm)" package="1206 [SMD]"]
  MIC1 = Microphone  # not connected
  SPKR1 = Loudspeaker  # not connected

nets:
  N1: Part1.A5/SCL, Raspberry_Pi1.5V
  N2: Part1.D10_PWM/SS, J2.pulse
  N3: Part1.D11_PWM/MOSI, J3.pulse
  N4: Part1.D5_PWM, Part1.D6_PWM, Part2.SIG
  GND: Part1.GND, Raspberry_Pi1.GND, Raspberry_Pi1.GPIO12, LED1.anode
  N5: Raspberry_Pi1.GPIO16, LED1.cathode
  N6: M1.Pin_1, BAT4.+
  N7: M1.Pin_2, BAT4.-
  N8: M1.Pin_3, Part2.V+
  N9: M2.pin_1, M3.pin_1, Part2.VIN
  N10: M2.pin_2, M3.pin_2, Part2.GND
  GND_2: J2.gnd, J3.gnd, BAT1.-
  VCC: J2.vcc, J3.vcc, BAT1.+
